// Logisim project w1_five_solve2.circ as structural Verilog: 1 circuit, main circuit main
module main (
  input  A,
  input  B,
  input  C,
  input  D,
  input  E,
  output out_6
);

  wire and_1_out, and_2_out, and_3_out, not_1_out, not_2_out, not_3_out, not_4_out;

  not not_1 (not_1_out, A);
  not not_2 (not_2_out, D);
  not not_3 (not_3_out, E);
  not not_4 (not_4_out, C);
  and and_1 (and_1_out, B, not_4_out, D);
  and and_2 (and_2_out, not_1_out, D);
  and and_3 (and_3_out, C, not_2_out, not_3_out);
  or or_1 (out_6, and_2_out, and_1_out, and_3_out);
endmodule
