// Logisim project w1_five_solve3.circ as structural Verilog: 1 circuit, main circuit main
module main (
  input  A,
  input  B,
  input  C,
  input  D,
  input  E,
  output out_6
);

  wire N1_out, N2_out, N3_out, N4_out, N5_out, N7_out, N8_out, N9_out, N10_out;

  not N7 (N7_out, C);
  not N1 (N1_out, D);
  not N4 (N4_out, E);
  nand N8 (N8_out, B, N7_out);
  nand N2 (N2_out, C, N1_out);
  not N3 (N3_out, N2_out);
  nand N9 (N9_out, A, N8_out);
  nand N5 (N5_out, N3_out, N4_out);
  nand N10 (N10_out, N9_out, D);
  nand N11 (out_6, N10_out, N5_out);
endmodule
