// Logisim project w1_nor_by_nand.circ as structural Verilog: 1 circuit, main circuit main
module main (
  input  A,
  input  B,
  output out_3
);

  wire nand_1_out, nand_2_out, nand_3_out;

  nand nand_1 (nand_1_out, A, A);
  nand nand_2 (nand_2_out, B, B);
  nand nand_3 (nand_3_out, nand_1_out, nand_2_out);
  nand nand_4 (out_3, nand_3_out, nand_3_out);
endmodule
