// Logisim project w2_1bit_full_adder.circ as structural Verilog: 1 circuit, main circuit main
module main (
  input  Cin,
  input  A,
  input  B,
  input  Cin_2,
  input  A_2,
  input  B_2,
  output Sum,
  output Carry,
  output Sum_2,
  output Carry_2
);

  wire and_1_out, and_2_out, and_3_out, nand_1_out, nand_2_out, nand_3_out, nand_4_out, nand_5_out,
       nand_6_out, nand_7_out, nand_9_out, nand_10_out, nand_11_out, nand_12_out, xor_1_out;

  nand nand_1 (nand_1_out, Cin_2, A_2);
  nand nand_2 (nand_2_out, Cin_2, B_2);
  nand nand_3 (nand_3_out, A_2, B_2);
  xor xor_1 (xor_1_out, Cin, A);
  and and_1 (and_1_out, Cin, A);
  and and_2 (and_2_out, A, B);
  and and_3 (and_3_out, Cin, B);
  nand nand_4 (nand_4_out, nand_2_out, nand_3_out);
  xor xor_2 (Sum, xor_1_out, B);
  or or_1 (Carry, and_1_out, and_2_out, and_3_out);
  nand nand_5 (nand_5_out, nand_4_out, nand_4_out);
  nand nand_6 (nand_6_out, Cin_2, nand_1_out);
  nand nand_7 (nand_7_out, nand_1_out, A_2);
  nand nand_8 (Carry_2, nand_1_out, nand_5_out);
  nand nand_9 (nand_9_out, nand_6_out, nand_7_out);
  nand nand_10 (nand_10_out, nand_9_out, B_2);
  nand nand_11 (nand_11_out, nand_9_out, nand_10_out);
  nand nand_12 (nand_12_out, nand_10_out, B_2);
  nand nand_13 (Sum_2, nand_11_out, nand_12_out);
endmodule
