// Logisim project w2_1bit_half_adder.circ as structural Verilog: 1 circuit, main circuit main
module main (
  input  A,
  input  B,
  input  I0,
  input  I1,
  output S,
  output C,
  output S_2,
  output C_2
);

  wire nand_1_out, nand_2_out, nand_3_out, nand_4_out;

  xor xor_1 (S, A, B);
  and and_1 (C, A, B);
  nand nand_1 (nand_1_out, I0, I1);
  nand nand_2 (nand_2_out, I0, I1);
  nand nand_3 (nand_3_out, I0, nand_1_out);
  nand nand_4 (nand_4_out, nand_1_out, I1);
  nand nand_5 (C_2, nand_2_out, nand_2_out);
  nand nand_6 (S_2, nand_3_out, nand_4_out);
endmodule
