// Logisim project w2_4bit_incrementer.circ as structural Verilog: 2 circuits, main circuit main
module main (
  input  [3:0] in_1,
  output [3:0] out_2
);

  wire w2_1bit_half_adder_1_c, w2_1bit_half_adder_2_c, w2_1bit_half_adder_3_c;

  w2_1bit_half_adder w2_1bit_half_adder_1 (.A(1'b1), .B(in_1[0]), .S(out_2[0]), .C(w2_1bit_half_adder_1_c));
  w2_1bit_half_adder w2_1bit_half_adder_2 (
    .A(w2_1bit_half_adder_1_c), .B(in_1[1]), .S(out_2[1]), .C(w2_1bit_half_adder_2_c));
  w2_1bit_half_adder w2_1bit_half_adder_3 (
    .A(w2_1bit_half_adder_2_c), .B(in_1[2]), .S(out_2[2]), .C(w2_1bit_half_adder_3_c));
  w2_1bit_half_adder w2_1bit_half_adder_4 (.A(w2_1bit_half_adder_3_c), .B(in_1[3]), .S(out_2[3]));  // open: C
endmodule

module w2_1bit_half_adder (
  input  A,
  input  B,
  output S,
  output C
);

  xor xor_1 (S, A, B);
  and and_1 (C, A, B);
endmodule
