// Logisim project w2_4bit_subtructor.circ as structural Verilog
module full_adder (
  input  Cin,
  input  A,
  input  B,
  output Sum,
  output Carry
);

  wire and_1_out, and_2_out, and_3_out, xor_1_out;

  xor xor_1 (xor_1_out, Cin, A);
  and and_1 (and_1_out, Cin, A);
  and and_2 (and_2_out, A, B);
  and and_3 (and_3_out, Cin, B);
  xor xor_2 (Sum, xor_1_out, B);
  or or_1 (Carry, and_1_out, and_2_out, and_3_out);
endmodule

module _4_bit_full_adder (
  input  [3:0] A,
  input  [3:0] B,
  output [3:0] Sum
);

  wire full_adder_1_carry, full_adder_2_carry, full_adder_3_carry;

  full_adder full_adder_1 (.A(A[0]), .B(B[0]), .Sum(Sum[0]), .Carry(full_adder_1_carry));  // open: Cin
  full_adder full_adder_2 (.Cin(full_adder_1_carry), .A(A[1]), .B(B[1]), .Sum(Sum[1]), .Carry(full_adder_2_carry));
  full_adder full_adder_3 (.Cin(full_adder_2_carry), .A(A[2]), .B(B[2]), .Sum(Sum[2]), .Carry(full_adder_3_carry));
  full_adder full_adder_4 (.Cin(full_adder_3_carry), .A(A[3]), .B(B[3]), .Sum(Sum[3]));  // open: Carry
endmodule
