// Logisim project w2_ALU.circ as structural Verilog: 5 circuits, main circuit main
module main (
  input  zx,
  input  nx,
  input  f,
  input  no,
  input  [3:0] x,
  input  zy,
  input  ny,
  input  [3:0] y,
  output [3:0] out,
  output zr,
  output ng
);

  wire not_3_out, not_4_out;
  wire [3:0] and_1_out, multiplexer_1_out, multiplexer_2_out, multiplexer_3_out, multiplexer_4_out,
       multiplexer_5_out, n4bit_full_adder_1_out, not_1_out, not_2_out, not_5_out, not_6_out, not_7_out;

  assign not_1_out = ~4'b1111;  // NOT_Gate not_1, 4 bits wide
  assign not_2_out = ~4'b1111;  // NOT_Gate not_2, 4 bits wide
  not not_3 (not_3_out, zx);
  multiplexer multiplexer_1 (.A(not_1_out), .B(x), .C(not_3_out), .out(multiplexer_1_out));
  not not_4 (not_4_out, zy);
  multiplexer multiplexer_2 (.A(not_2_out), .B(y), .C(not_4_out), .out(multiplexer_2_out));
  assign not_5_out = ~multiplexer_1_out;  // NOT_Gate not_5, 4 bits wide
  assign not_6_out = ~multiplexer_2_out;  // NOT_Gate not_6, 4 bits wide
  multiplexer multiplexer_3 (.A(multiplexer_1_out), .B(not_5_out), .C(nx), .out(multiplexer_3_out));
  multiplexer multiplexer_4 (.A(multiplexer_2_out), .B(not_6_out), .C(ny), .out(multiplexer_4_out));
  assign and_1_out = multiplexer_3_out & multiplexer_4_out;  // AND_Gate and_1, 4 bits wide
  _4bit_full_adder u_4bit_full_adder_1 (.A(multiplexer_3_out), .B(multiplexer_4_out), .out(n4bit_full_adder_1_out));
  multiplexer multiplexer_5 (.A(and_1_out), .B(n4bit_full_adder_1_out), .C(f), .out(multiplexer_5_out));
  assign not_7_out = ~multiplexer_5_out;  // NOT_Gate not_7, 4 bits wide
  multiplexer multiplexer_6 (.A(multiplexer_5_out), .B(not_7_out), .C(no), .out(out));
  comparison comparison_1 (.in(out), .zr(zr), .ng(ng));
endmodule

module full_adder (
  input  Cin,
  input  A,
  input  B,
  output Sum,
  output Carry
);

  wire and_1_out, and_2_out, and_3_out, xor_1_out;

  xor xor_1 (xor_1_out, Cin, A);
  and and_1 (and_1_out, Cin, A);
  and and_2 (and_2_out, A, B);
  and and_3 (and_3_out, Cin, B);
  xor xor_2 (Sum, xor_1_out, B);
  or or_1 (Carry, and_1_out, and_2_out, and_3_out);
endmodule

module multiplexer (
  input  C,
  input  [3:0] A,
  input  [3:0] B,
  output [3:0] out
);

  wire [3:0] and_1_out, and_2_out;
  wire [3:3] not_1_out;

  not not_1 (not_1_out[3], C);
  assign and_1_out = {4{not_1_out[3]}} & A;  // AND_Gate and_1, 4 bits wide
  assign and_2_out = {4{C}} & B;  // AND_Gate and_2, 4 bits wide
  assign out = and_1_out | and_2_out;  // OR_Gate or_1, 4 bits wide
endmodule

module _4bit_full_adder (
  input  [3:0] A,
  input  [3:0] B,
  output [3:0] out
);

  wire full_adder_1_carry, full_adder_2_carry, full_adder_3_carry, not_1_out;

  not not_1 (not_1_out, 1'b1);
  full_adder full_adder_1 (.Cin(not_1_out), .A(A[0]), .B(B[0]), .Sum(out[0]), .Carry(full_adder_1_carry));
  full_adder full_adder_2 (.Cin(full_adder_1_carry), .A(A[1]), .B(B[1]), .Sum(out[1]), .Carry(full_adder_2_carry));
  full_adder full_adder_3 (.Cin(full_adder_2_carry), .A(A[2]), .B(B[2]), .Sum(out[2]), .Carry(full_adder_3_carry));
  full_adder full_adder_4 (.Cin(full_adder_3_carry), .A(A[3]), .B(B[3]), .Sum(out[3]));  // open: Carry
endmodule

module comparison (
  input  [3:0] in,
  output zr,
  output ng
);

  wire not_1_out, not_2_out, not_3_out, not_4_out;

  not not_1 (not_1_out, in[0]);
  not not_2 (not_2_out, in[1]);
  not not_3 (not_3_out, in[2]);
  not not_4 (not_4_out, in[3]);
  and and_1 (zr, not_1_out, not_2_out, not_3_out, not_4_out);

  assign ng = in[3];
endmodule
