// Logisim project w2_plexer.circ as structural Verilog: 3 circuits, main circuit main
module multiplexer (
  input  C1,
  input  C0,
  input  A,
  input  B,
  input  C,
  input  D,
  output out
);

  wire and_1_out, and_2_out, and_3_out, and_4_out, not_1_out, not_2_out;

  not not_1 (not_1_out, C1);
  not not_2 (not_2_out, C0);
  and and_1 (and_1_out, not_2_out, not_1_out, A);
  and and_2 (and_2_out, C0, not_1_out, B);
  and and_3 (and_3_out, not_2_out, C1, C);
  and and_4 (and_4_out, C0, C1, D);
  or or_1 (out, and_1_out, and_2_out, and_3_out, and_4_out);
endmodule

module main (
  input  [1:0] C,
  input  A,
  input  D,
  input  B,
  output out_5
);

  wire and_1_out, multiplexer_1_out, nor_1_out, or_1_out, xor_1_out;

  and and_1 (and_1_out, A, B);
  or or_1 (or_1_out, A, B);
  xor xor_1 (xor_1_out, A, B);
  nor nor_1 (nor_1_out, A, B);
  multiplexer multiplexer_1 (
    .A(and_1_out), .B(or_1_out), .C(xor_1_out), .D(nor_1_out), .C1(C[1]), .C0(C[0]), .out(multiplexer_1_out));
  demultiplexer demultiplexer_1 (.E(multiplexer_1_out), .D(D), .out(out_5));
endmodule

module demultiplexer (
  input  D,
  input  E,
  output out
);

  wire not_1_out;

  not not_1 (not_1_out, D);
  and and_1 (out, not_1_out, E);
endmodule
