// Logisim project w3_8word_RAM.circ as structural Verilog: 8 circuits, main circuit main
module main (
  input  load,
  input  [2:0] address,
  input  [15:0] in,
  output [15:0] out
);

  wire CLK_out;

  _16bit_register u_16bit_register_1 (.in(in), .load(load), .CLK(CLK_out));  // open: out
  _16bit_register u_16bit_register_2 (.in(in), .load(load), .CLK(CLK_out));  // open: out
  _16bit_register u_16bit_register_3 (.in(in), .load(load), .CLK(CLK_out));  // open: out
  _16bit_register u_16bit_register_4 (.in(in), .load(load), .CLK(CLK_out));  // open: out
  Clock CLK (.out(CLK_out));
  _16bit_register u_16bit_register_5 (.in(in), .load(load), .CLK(CLK_out));  // open: out
  _16bit_register u_16bit_register_6 (.in(in), .load(load), .CLK(CLK_out));  // open: out
  _16bit_register u_16bit_register_7 (.in(in), .load(load), .CLK(CLK_out));  // open: out
  _16bit_register u_16bit_register_8 (.in(in), .load(load), .CLK(CLK_out));  // open: out
endmodule

module RS (
  input  R,
  input  S,
  output Q,
  output nQ
);

  nand nand_1 (Q, R, nQ);
  nand nand_2 (nQ, Q, S);
endmodule

module D (
  input  en,
  input  D,
  output Q,
  output nQ
);

  wire nand_1_out, nand_2_out, not_1_out;

  not not_1 (not_1_out, D);
  nand nand_1 (nand_1_out, en, not_1_out);
  nand nand_2 (nand_2_out, en, D);
  RS rs_1 (.R(nand_1_out), .Q(Q), .nQ(nQ), .S(nand_2_out));
endmodule

module multiplexer (
  input  Sel,
  input  A,
  input  B,
  output O
);

  wire and_1_out, and_2_out, not_1_out;

  not not_1 (not_1_out, Sel);
  and and_1 (and_1_out, not_1_out, A);
  and and_2 (and_2_out, Sel, B);
  or or_1 (O, and_1_out, and_2_out);
endmodule

module DFF (
  input  CLK,
  input  D,
  output Q,
  output nQ
);

  wire d_1_q, not_1_out;

  not not_1 (not_1_out, CLK);
  D d_1 (.en(not_1_out), .Q(d_1_q), .D(D));  // open: nQ
  D d_2 (.en(CLK), .Q(Q), .nQ(nQ), .D(d_1_q));
endmodule

module _1bit_register (
  input  load,
  input  CLK,
  input  in,
  output O
);

  wire multiplexer_1_o;

  multiplexer multiplexer_1 (.A(O), .B(in), .Sel(load), .O(multiplexer_1_o));
  DFF dff_1 (.CLK(CLK), .D(multiplexer_1_o), .Q(O));  // open: nQ
endmodule

module _16bit_register (
  input  load,
  input  [15:0] in,
  input  CLK,
  output [15:0] out
);

  _1bit_register _0 (.in(in[0]), .O(out[0]), .load(load), .CLK(CLK));
  _1bit_register _2 (.in(in[2]), .O(out[2]), .load(load), .CLK(CLK));
  _1bit_register _4 (.in(in[4]), .O(out[4]), .load(load), .CLK(CLK));
  _1bit_register _6 (.in(in[6]), .O(out[6]), .load(load), .CLK(CLK));
  _1bit_register _8 (.in(in[8]), .O(out[8]), .load(load), .CLK(CLK));
  _1bit_register _10 (.in(in[10]), .O(out[10]), .load(load), .CLK(CLK));
  _1bit_register _12 (.in(in[12]), .O(out[12]), .load(load), .CLK(CLK));
  _1bit_register _14 (.in(in[14]), .O(out[14]), .load(load), .CLK(CLK));
  _1bit_register _1 (.in(in[1]), .O(out[1]), .load(load), .CLK(CLK));
  _1bit_register _3 (.in(in[3]), .O(out[3]), .load(load), .CLK(CLK));
  _1bit_register _5 (.in(in[5]), .O(out[5]), .load(load), .CLK(CLK));
  _1bit_register _7 (.in(in[7]), .O(out[7]), .load(load), .CLK(CLK));
  _1bit_register _9 (.in(in[9]), .O(out[9]), .load(load), .CLK(CLK));
  _1bit_register _11 (.in(in[11]), .O(out[11]), .load(load), .CLK(CLK));
  _1bit_register _13 (.in(in[13]), .O(out[13]), .load(load), .CLK(CLK));
  _1bit_register _15 (.in(in[15]), .O(out[15]), .load(load), .CLK(CLK));
endmodule

module address_plexer (
  input  [2:0] address,
  input  [15:0] _0,
  input  [15:0] _1,
  input  [15:0] _2,
  input  [15:0] _3,
  input  [15:0] _4,
  input  [15:0] _5,
  input  [15:0] _6,
  input  [15:0] _7,
  output [15:0] out_10
);

  wire _001_out, _010_out, _011_out, _100_out, _101_out, _110_out, _111_out, not_1_out, not_2_out, not_3_out;
  wire [15:0] and_1_out;
  wire [15:15] _000_out;

  not not_1 (not_1_out, address[2]);
  not not_2 (not_2_out, address[0]);
  not not_3 (not_3_out, address[1]);
  and _000 (_000_out[15], not_2_out, not_3_out, not_1_out);
  and _001 (_001_out, not_1_out, not_3_out, address[0]);
  and _010 (_010_out, not_1_out, address[1], not_2_out);
  and _011 (_011_out, not_1_out, address[1], address[0]);
  and _100 (_100_out, address[2], not_3_out, not_2_out);
  and _101 (_101_out, address[2], not_3_out, address[0]);
  and _110 (_110_out, address[2], address[1], not_2_out);
  and _111 (_111_out, address[2], address[1], address[0]);
  assign and_1_out = _0 & {16{_000_out[15]}};  // AND_Gate and_1, 16 bits wide
  assign out_10 = and_1_out;  // OR_Gate or_1, 16 bits wide OR_Gate
endmodule
