// Logisim project w4_counter.circ as structural Verilog: 1 circuit, main circuit main
module main (
  input  [15:0] in_1,
  input  in_2,
  input  in_3,
  input  in_4,
  output [15:0] out_5
);

  wire clock_1_out, clock_2_out, or_1_out;
  wire [15:0] adder_1_out, multiplexer_1_out, multiplexer_2_out, multiplexer_3_out, register_1_q;

  Adder #(.width(16)) adder_1 (.a(multiplexer_3_out), .b(16'h1), .out(adder_1_out));  // open: cin, cout
  Multiplexer #(.width(16)) multiplexer_1 (
    .in0(in_1), .in1(adder_1_out), .out(multiplexer_1_out), .sel(in_4));  // open: en
  Register #(.width(16)) register_1 (
    .D(multiplexer_1_out), .en(1'b1), .Q(register_1_q), .clk(clock_1_out));  // open: clr
  Clock clock_1 (.out(clock_1_out));
  Multiplexer #(.width(16)) multiplexer_2 (
    .in0(register_1_q), .in1(in_1), .out(multiplexer_2_out), .sel(in_3));  // open: en
  Multiplexer #(.width(16)) multiplexer_3 (
    .in0(multiplexer_2_out), .in1({16{1'b0}}), .out(multiplexer_3_out), .sel(in_2));  // open: en
  or or_1 (or_1_out, in_2, in_3, in_4);
  Register #(.width(16)) register_2 (.D(multiplexer_3_out), .en(or_1_out), .Q(out_5), .clk(clock_2_out));  // open: clr
  Clock clock_2 (.out(clock_2_out));
endmodule
