// Logisim project w4_transitors.circ as structural Verilog: 1 circuit, main circuit main
module main (
  input  in_1,
  input  in_2,
  input  in_3,
  input  in_4,
  input  in_5,
  output out_6,
  output out_7,
  output out_8
);

  wire transistor_3_out, transistor_4_out, transistor_9_out, transistor_12_out;

  Transistor transistor_1 (.in(1'b1), .out(out_6), .gate(in_1));
  Transistor #(.\type ("n")) transistor_2 (.in(1'b0), .out(out_6), .gate(in_1));
  Transistor #(.\type ("n")) transistor_3 (.in(1'b0), .out(transistor_3_out), .gate(in_4));
  Transistor transistor_4 (.in(1'b1), .out(transistor_4_out), .gate(in_5));
  Transistor transistor_5 (.in(transistor_4_out), .out(transistor_3_out), .gate(in_4));
  Transistor #(.\type ("n")) transistor_6 (.in(1'b0), .out(transistor_3_out), .gate(in_5));
  Transistor transistor_7 (.in(1'b1), .out(out_8), .gate(transistor_3_out));
  Transistor #(.\type ("n")) transistor_8 (.in(1'b0), .out(out_8), .gate(transistor_3_out));
  Transistor transistor_9 (.in(1'b1), .out(transistor_9_out), .gate(in_3));
  Transistor transistor_10 (.in(1'b1), .out(transistor_9_out), .gate(in_2));
  Transistor #(.\type ("n")) transistor_11 (.in(transistor_12_out), .out(transistor_9_out), .gate(in_2));
  Transistor #(.\type ("n")) transistor_12 (.in(1'b0), .out(transistor_12_out), .gate(in_3));
  Transistor transistor_13 (.in(1'b1), .out(out_7), .gate(transistor_9_out));
  Transistor #(.\type ("n")) transistor_14 (.in(1'b0), .out(out_7), .gate(transistor_9_out));
endmodule
