// Logisim project w1_five_solve1.circ as structural Verilog: 1 circuit, main circuit main
module main (
  input  A,
  input  B,
  input  C,
  input  D,
  input  E,
  output out_6
);

  wire and_1_out, and_2_out, and_3_out, and_4_out, and_5_out, and_6_out, not_1_out, not_2_out, not_3_out,
       not_4_out, or_1_out, or_2_out;

  not not_1 (not_1_out, C);
  not not_2 (not_2_out, D);
  and and_1 (and_1_out, B, not_1_out);
  and and_2 (and_2_out, C, not_2_out);
  not not_3 (not_3_out, E);
  and and_3 (and_3_out, and_1_out, D);
  and and_4 (and_4_out, and_2_out, not_3_out);
  or or_1 (or_1_out, and_4_out, D);
  or or_2 (or_2_out, and_3_out, and_4_out);
  not not_4 (not_4_out, A);
  and and_5 (and_5_out, A, or_2_out);
  and and_6 (and_6_out, not_4_out, or_1_out);
  or or_3 (out_6, and_5_out, and_6_out);
endmodule
