// Logisim project w2_4bit_full_adder.circ as structural Verilog: 2 circuits, main circuit main
module main (
  input  [3:0] in_1,
  input  [3:0] in_2,
  output [3:0] out_3
);

  wire full_adder_1_carry, full_adder_2_carry, full_adder_3_carry, not_1_out;

  not not_1 (not_1_out, 1'b1);
  full_adder full_adder_1 (.Cin(not_1_out), .A(in_1[0]), .B(in_2[0]), .Sum(out_3[0]), .Carry(full_adder_1_carry));
  full_adder full_adder_2 (
    .Cin(full_adder_1_carry), .A(in_1[1]), .B(in_2[1]), .Sum(out_3[1]), .Carry(full_adder_2_carry));
  full_adder full_adder_3 (
    .Cin(full_adder_2_carry), .A(in_1[2]), .B(in_2[2]), .Sum(out_3[2]), .Carry(full_adder_3_carry));
  full_adder full_adder_4 (.Cin(full_adder_3_carry), .A(in_1[3]), .B(in_2[3]), .Sum(out_3[3]));  // open: Carry
endmodule

module full_adder (
  input  Cin,
  input  A,
  input  B,
  output Sum,
  output Carry
);

  wire and_1_out, and_2_out, and_3_out, xor_1_out;

  xor xor_1 (xor_1_out, Cin, A);
  and and_1 (and_1_out, Cin, A);
  and and_2 (and_2_out, A, B);
  and and_3 (and_3_out, Cin, B);
  xor xor_2 (Sum, xor_1_out, B);
  or or_1 (Carry, and_1_out, and_2_out, and_3_out);
endmodule
