// Logisim project w2_4bit_subtructor.circ as structural Verilog: 4 circuits, main circuit main
module main (
  input  Select,
  input  [3:0] A,
  input  [3:0] B,
  output [3:0] out
);

  wire [3:0] A_B_2_sum, A_B_sum, not_4_out, not_B_1_sum;
  wire [3:1] not_1_out;

  not not_1 (not_1_out[1], 1'b1);
  not not_2 (not_1_out[2], 1'b1);
  not not_3 (not_1_out[3], 1'b1);
  _4_bit_full_adder A_B (.A(A), .B(B), .Sum(A_B_sum));
  assign not_4_out = ~B;  // NOT_Gate not_4, 4 bits wide
  _4_bit_full_adder not_B_1 (.A(not_4_out), .B({not_1_out, 1'b1}), .Sum(not_B_1_sum));
  _4_bit_full_adder A_B_2 (.A(A), .B(not_B_1_sum), .Sum(A_B_2_sum));
  multiplexer multiplexer_1 (.A(A_B_sum), .B(A_B_2_sum), .select(Select), .Out(out));
endmodule

module full_adder (
  input  Cin,
  input  A,
  input  B,
  output Sum,
  output Carry
);

  wire and_1_out, and_2_out, and_3_out, xor_1_out;

  xor xor_1 (xor_1_out, Cin, A);
  and and_1 (and_1_out, Cin, A);
  and and_2 (and_2_out, A, B);
  and and_3 (and_3_out, Cin, B);
  xor xor_2 (Sum, xor_1_out, B);
  or or_1 (Carry, and_1_out, and_2_out, and_3_out);
endmodule

module _4_bit_full_adder (
  input  [3:0] A,
  input  [3:0] B,
  output [3:0] Sum
);

  wire full_adder_1_carry, full_adder_2_carry, full_adder_3_carry, not_1_out;

  not not_1 (not_1_out, 1'b1);
  full_adder full_adder_1 (.Cin(not_1_out), .A(A[0]), .B(B[0]), .Sum(Sum[0]), .Carry(full_adder_1_carry));
  full_adder full_adder_2 (.Cin(full_adder_1_carry), .A(A[1]), .B(B[1]), .Sum(Sum[1]), .Carry(full_adder_2_carry));
  full_adder full_adder_3 (.Cin(full_adder_2_carry), .A(A[2]), .B(B[2]), .Sum(Sum[2]), .Carry(full_adder_3_carry));
  full_adder full_adder_4 (.Cin(full_adder_3_carry), .A(A[3]), .B(B[3]), .Sum(Sum[3]));  // open: Carry
endmodule

module multiplexer (
  input  select,
  input  [3:0] A,
  input  [3:0] B,
  output [3:0] Out
);

  wire [3:0] and_1_out, and_2_out;
  wire [3:3] not_1_out;

  not not_1 (not_1_out[3], select);
  assign and_1_out = {4{not_1_out[3]}} & A;  // AND_Gate and_1, 4 bits wide
  assign and_2_out = {4{select}} & B;  // AND_Gate and_2, 4 bits wide
  assign Out = and_1_out | and_2_out;  // OR_Gate or_1, 4 bits wide
endmodule
