// Logisim project w3_shift_register.circ as structural Verilog: 2 circuits, main circuit main
module main (
  input  shift,
  input  rorate,
  input  [15:0] in_3,
  input  load,
  output [15:0] out_5
);

  wire clock_1_out, or_1_out;
  wire [15:0] multiplexer_1_out;

  Multiplexer #(.select(2), .width(16)) multiplexer_1 (
    .in0(in_3), .in1(in_3), .in2({out_5[14:0], 1'b0}), .in3({out_5[14:0], out_5[15]}),
    .out(multiplexer_1_out), .sel({rorate, shift}));  // open: en
  or or_1 (or_1_out, shift, load);
  Register #(.width(16)) register_1 (.D(multiplexer_1_out), .en(or_1_out), .Q(out_5), .clk(clock_1_out));  // open: clr
  Clock clock_1 (.out(clock_1_out));
endmodule

module _16_bit_shift_register (
  input  [15:0] in_1,
  input  [3:0] shift,
  input  load,
  output [15:0] out_4
);

  wire clock_1_out, or_1_out;
  wire [15:0] multiplexer_1_out, multiplexer_2_out, multiplexer_3_out, multiplexer_4_out, multiplexer_5_out;

  or or_1 (or_1_out, shift[0], shift[1], shift[2], shift[3]);
  Multiplexer #(.width(16)) multiplexer_1 (
    .in0(in_1), .in1(multiplexer_5_out), .out(multiplexer_1_out), .sel(or_1_out));  // open: en
  Multiplexer #(.width(16)) multiplexer_2 (
    .in0(out_4), .in1({out_4[14:0], out_4[15]}), .out(multiplexer_2_out), .sel(shift[0]));  // open: en
  Multiplexer #(.width(16)) multiplexer_3 (
    .in0(multiplexer_2_out), .in1({multiplexer_2_out[13:0], multiplexer_2_out[15:14]}),
    .out(multiplexer_3_out), .sel(shift[1]));  // open: en
  Multiplexer #(.width(16)) multiplexer_4 (
    .in0(multiplexer_3_out), .in1({multiplexer_3_out[11:0], multiplexer_3_out[15:12]}),
    .out(multiplexer_4_out), .sel(shift[2]));  // open: en
  Multiplexer #(.width(16)) multiplexer_5 (
    .in0(multiplexer_4_out), .in1({multiplexer_4_out[7:0], multiplexer_4_out[15:8]}),
    .out(multiplexer_5_out), .sel(shift[3]));  // open: en
  Clock clock_1 (.out(clock_1_out));
  Register #(.width(16)) register_1 (.D(multiplexer_1_out), .en(load), .Q(out_4), .clk(clock_1_out));  // open: clr
endmodule
