// Logisim project w4_risefall.circ as structural Verilog
module one_shot (
  input  in,
  output out
);

  wire and_1_out, CLK_out, not_1_out, register_1_q;

  not not_1 (not_1_out, register_1_q);
  and and_1 (and_1_out, not_1_out, in);
  Clock CLK (.out(CLK_out));
  Register #(.width(1)) register_1 (.D(in), .en(1'b1), .Q(register_1_q), .clk(CLK_out));  // open: clr
  Register #(.width(1)) register_2 (.D(and_1_out), .en(1'b1), .Q(out), .clk(CLK_out));  // open: clr
endmodule

module rise_fall (
  input  in,
  output rise,
  output fall
);

  wire not_1_out;

  not not_1 (not_1_out, in);
  one_shot one_shot_1 (.in(in), .out(rise));
  one_shot one_shot_2 (.in(not_1_out), .out(fall));
endmodule

module rise_fall_mealy (
  input  in_1,
  output rise,
  output fall
);

  wire and_1_out, and_2_out, clock_1_out, not_1_out, not_2_out, register_1_q;

  not not_1 (not_1_out, register_1_q);
  and and_1 (and_1_out, not_1_out, in_1);
  and and_2 (and_2_out, register_1_q, not_2_out);
  not not_2 (not_2_out, in_1);
  Register #(.width(1)) register_1 (.D(in_1), .en(1'b1), .Q(register_1_q), .clk(clock_1_out));  // open: clr
  Register #(.width(1)) register_2 (.D(and_1_out), .en(1'b1), .Q(rise), .clk(clock_1_out));  // open: clr
  Register #(.width(1)) register_3 (.D(and_2_out), .en(1'b1), .Q(fall), .clk(clock_1_out));  // open: clr
  Clock clock_1 (.out(clock_1_out));
endmodule
